// Logisim project GshareGiven.circ as structural Verilog: 5 circuits, main circuit main
module main (
);

  wire Clock, Correct, CorrectPred, Done, gsharepredictor_1_takebranch, inputgen_1_branchtaken,
       inputgen_1_isbranch, IsPredBranchCorrect, IsPredCorrect, not_1_out;
  wire [31:0] CorrectPredBranch, gsharepredictor_1_predbranchdest, inputgen_1_branchdestaddress,
       inputgen_1_predpc, inputgen_1_updatepc;

  InputGen inputgen_1 (
    .Clock(Clock), .PredPC(inputgen_1_predpc), .UpdatePC(inputgen_1_updatepc),
    .IsBranch(inputgen_1_isbranch), .BranchTaken(inputgen_1_branchtaken),
    .BranchDestAddress(inputgen_1_branchdestaddress));
  GsharePredictor gsharepredictor_1 (
    .PredPC(inputgen_1_predpc), .UpdatePC(inputgen_1_updatepc), .IsBranch(inputgen_1_isbranch),
    .BranchTaken(inputgen_1_branchtaken), .BranchDestAddr(inputgen_1_branchdestaddress), .Clock(Clock),
    .TakeBranch(gsharepredictor_1_takebranch), .PredBranchDest(gsharepredictor_1_predbranchdest));
  Clock clock_1 (.out(Clock));
  Test test_1 (
    .TakeBranch(gsharepredictor_1_takebranch), .PredBranchAddress(gsharepredictor_1_predbranchdest),
    .Clock(Clock), .IsPredCorrect(IsPredCorrect), .CorrectPred(CorrectPred),
    .IsPredBranchCorrect(IsPredBranchCorrect), .CorrectPredBranch(CorrectPredBranch), .Correct(Correct),
    .Done(Done));
  not not_1 (not_1_out, Done);
  Shift_Register #(.length(28)) shift_register_1 (
    .shift(not_1_out), .in(Correct), .clk(Clock));  // open: out, load, clr, d0, q0, d1, q1, d2, q2, d3, q3, d4, q4, d5, q5, d6, q6, d7, q7, d8, q8, d9, q9, d10, q10, d11, q11, d12, q12, d13, q13, d14, q14, d15, q15, d16, q16, d17, q17, d18, q18, d19, q19, d20, q20, d21, q21, d22, q22, d23, q23, d24, q24, d25, q25, d26, q26, d27, q27
  // Probe on IsPredCorrect
  // Probe on CorrectPred
  // Probe on IsPredBranchCorrect
  // Probe on CorrectPredBranch
  // Probe on Correct
  // Probe on Done
endmodule

module GsharePredictor (
  input  [31:0] PredPC,
  input  [31:0] UpdatePC,
  input  IsBranch,
  input  BranchTaken,
  input  [31:0] BranchDestAddr,
  input  Clock,
  output TakeBranch,
  output [31:0] PredBranchDest
);

  wire _0, _1, and_1_out, and_2_out, and_3_out, and_4_out, and_6_out, and_7_out, and_8_out, and_9_out,
       counter_1_ohalf, counter_2_ohalf, counter_3_ohalf, counter_4_ohalf, CounterTaken, CS0, CS1, CS2, CS3,
       TagCorrect, tunnel, tunnel_t;
  wire [1:0] BHR, Index;
  wire [31:0] BDR_2_q, BDR_3_q, BDR_4_q, BDR_q, multiplexer_1_out, Tag_Register_2_q, Tag_Register_3_q,
       Tag_Register_4_q, Tag_Register_q, xor_1_out;

  and and_1 (and_1_out, IsBranch, CS0);
  and and_2 (and_2_out, IsBranch, CS1);
  and and_3 (and_3_out, IsBranch, CS2);
  and and_4 (and_4_out, IsBranch, CS3);
  Register #(.width(32)) Tag_Register (.D(UpdatePC), .en(and_1_out), .Q(Tag_Register_q), .clk(Clock));  // open: clr
  Register #(.width(32)) Tag_Register_2 (.D(UpdatePC), .en(and_2_out), .Q(Tag_Register_2_q), .clk(Clock));  // open: clr
  Register #(.width(32)) Tag_Register_3 (.D(UpdatePC), .en(and_3_out), .Q(Tag_Register_3_q), .clk(Clock));  // open: clr
  Register #(.width(32)) Tag_Register_4 (.D(UpdatePC), .en(and_4_out), .Q(Tag_Register_4_q), .clk(Clock));  // open: clr
  Multiplexer #(.select(2), .width(32), .enable("false")) multiplexer_1 (
    .in0(Tag_Register_q), .in1(Tag_Register_2_q), .in2(Tag_Register_3_q), .in3(Tag_Register_4_q),
    .out(multiplexer_1_out), .sel(Index));
  assign xor_1_out = PredPC ^ multiplexer_1_out;  // XOR_Gate xor_1, 32 bits wide
  Shift_Register #(.length(2)) Branch_History_Register (
    .shift(IsBranch), .in(BranchTaken), .clk(Clock), .q0(BHR[1]), .q1(BHR[0]));  // open: out, load, clr, d0, d1
  Counter counter_1 (
    ._1(_1), ._0(_0), .Enable(CS0), .CountUp(tunnel), .CountDn(tunnel_t), .Clock(Clock),
    .OHalf(counter_1_ohalf));
  Counter counter_2 (
    ._1(_1), ._0(_0), .Enable(CS1), .CountUp(tunnel), .CountDn(tunnel_t), .Clock(Clock),
    .OHalf(counter_2_ohalf));
  Counter counter_3 (
    ._1(_1), ._0(_0), .Enable(CS2), .CountUp(tunnel), .CountDn(tunnel_t), .Clock(Clock),
    .OHalf(counter_3_ohalf));
  Counter counter_4 (
    ._1(_1), ._0(_0), .Enable(CS3), .CountUp(tunnel), .CountDn(tunnel_t), .Clock(Clock),
    .OHalf(counter_4_ohalf));
  Multiplexer #(.select(2), .enable("false")) multiplexer_2 (
    .in0(counter_1_ohalf), .in1(counter_2_ohalf), .in2(counter_3_ohalf), .in3(counter_4_ohalf),
    .out(CounterTaken), .sel(Index));
  nor nor_1 (TagCorrect, xor_1_out[0], xor_1_out[1], xor_1_out[2], xor_1_out[3], xor_1_out[4], xor_1_out[5], xor_1_out[6], xor_1_out[7], xor_1_out[8], xor_1_out[9], xor_1_out[10], xor_1_out[11], xor_1_out[12], xor_1_out[13], xor_1_out[14], xor_1_out[15], xor_1_out[16], xor_1_out[17], xor_1_out[18], xor_1_out[19], xor_1_out[20], xor_1_out[21], xor_1_out[22], xor_1_out[23], xor_1_out[24], xor_1_out[25], xor_1_out[26], xor_1_out[27], xor_1_out[28], xor_1_out[29], xor_1_out[30], xor_1_out[31]);
  assign Index = PredPC[1:0] ^ BHR;  // XOR_Gate xor_2, 2 bits wide
  and and_5 (TakeBranch, CounterTaken, TagCorrect);
  Demultiplexer #(.select(2), .enable("false")) demultiplexer_1 (
    .out0(CS0), .out1(CS1), .out2(CS2), .out3(CS3), .in(1'b1), .sel(Index));
  and and_6 (and_6_out, IsBranch, CS0);
  and and_7 (and_7_out, IsBranch, CS1);
  and and_8 (and_8_out, IsBranch, CS2);
  and and_9 (and_9_out, IsBranch, CS3);
  and and_10 (tunnel_t, IsBranch, ~BranchTaken, TagCorrect);  // AND_Gate
  and and_11 (tunnel, IsBranch, BranchTaken, TagCorrect);
  and and_12 (_0, IsBranch, ~BranchTaken, ~TagCorrect);  // AND_Gate
  and and_13 (_1, IsBranch, BranchTaken, ~TagCorrect);  // AND_Gate
  Register #(.width(32)) BDR (.D(BranchDestAddr), .en(and_6_out), .Q(BDR_q), .clk(Clock));  // open: clr
  Register #(.width(32)) BDR_2 (.D(BranchDestAddr), .en(and_7_out), .Q(BDR_2_q), .clk(Clock));  // open: clr
  Register #(.width(32)) BDR_3 (.D(BranchDestAddr), .en(and_8_out), .Q(BDR_3_q), .clk(Clock));  // open: clr
  Register #(.width(32)) BDR_4 (.D(BranchDestAddr), .en(and_9_out), .Q(BDR_4_q), .clk(Clock));  // open: clr
  Multiplexer #(.width(32), .enable("false")) multiplexer_3 (
    .in0(BranchDestAddr), .in1(PredBranchDest), .sel(TakeBranch));  // open: out
  Multiplexer #(.select(2), .width(32), .enable("false")) multiplexer_4 (
    .in0(BDR_q), .in1(BDR_2_q), .in2(BDR_3_q), .in3(BDR_4_q), .out(PredBranchDest), .sel(Index));

  // Other names for the same wires on the sheet: BDA[31:0] = BranchDestAddr; BT = BranchTaken; IB = IsBranch;
  //   PBD[31:0] = PredBranchDest; PredictTaken = TakeBranch; PPCm[1:0] = PredPC[1:0]; Tag[31:0] = PredPC;
  //   UTag[31:0] = UpdatePC
endmodule

module InputGen (
  input  Clock,
  output [31:0] PredPC,
  output [31:0] UpdatePC,
  output IsBranch,
  output BranchTaken,
  output [31:0] BranchDestAddress
);

  wire [7:0] counter_1_q;

  Counter_part #(.max('h1b), .ongoal("stay")) counter_1 (
    .count(1'b1), .Q(counter_1_q), .clk(Clock));  // open: load, D, carry, clr
  ROM #(.dataWidth(32)) rom_1 (.addr(counter_1_q), .data(PredPC));  // open: sel
  ROM #(.dataWidth(1)) rom_2 (.addr(counter_1_q), .data(IsBranch));  // open: sel
  ROM #(.dataWidth(1)) rom_3 (.addr(counter_1_q), .data(BranchTaken));  // open: sel
  ROM #(.dataWidth(32)) rom_4 (.addr(counter_1_q), .data(BranchDestAddress));  // open: sel

  assign UpdatePC = PredPC;

  // Notes on the sheet:
  //   Counter max count is 27 because there are only 28 instructions
  //   contents of rom_1 (hex, n*v repeats v):
  //   5*0 1 1 1 5 2 2 2 3 3 3 0 0 4
  //   contents of rom_2 (hex, n*v repeats v):
  //   8*1 0 8*1 0 10*1
  //   contents of rom_3 (hex, n*v repeats v):
  //   8*1 0 6*1 4*0 1 0 1 0 1 0 1 0 1
  //   contents of rom_4 (hex, n*v repeats v):
  //   5*60 5f 5f 5f 0 5 5 5 8 8 8 60 60 0 10*60
endmodule

module Test (
  input  TakeBranch,
  input  [31:0] PredBranchAddress,
  input  Clock,
  output IsPredCorrect,
  output CorrectPred,
  output IsPredBranchCorrect,
  output [31:0] CorrectPredBranch,
  output Correct,
  output Done
);

  wire comparator_1_eq, comparator_2_eq, DontCare, not_1_out;
  wire [7:0] Count;

  Counter_part #(.max('h1c), .ongoal("stay")) counter_1 (
    .count(1'b1), .Q(Count), .clk(Clock));  // open: load, D, carry, clr
  ROM #(.dataWidth(1)) rom_1 (.addr(Count), .data(CorrectPred));  // open: sel
  ROM #(.dataWidth(32)) rom_2 (.addr(Count), .data(CorrectPredBranch));  // open: sel
  ROM #(.dataWidth(1)) rom_3 (.addr(Count), .data(DontCare));  // open: sel
  not not_1 (not_1_out, CorrectPred);
  Comparator #(.width(1), .mode("unsigned")) comparator_1 (
    .a(TakeBranch), .b(CorrectPred), .eq(comparator_1_eq));  // open: gt, lt
  or or_1 (IsPredCorrect, comparator_1_eq, DontCare);
  Comparator #(.width(32), .mode("unsigned")) comparator_2 (
    .a(PredBranchAddress), .b(CorrectPredBranch), .eq(comparator_2_eq));  // open: gt, lt
  Comparator #(.mode("unsigned")) comparator_3 (.a(Count), .b(8'h1c), .eq(Done));  // open: gt, lt
  // Probe on Count
  or or_2 (IsPredBranchCorrect, comparator_2_eq, not_1_out, DontCare);
  and and_1 (Correct, IsPredCorrect, IsPredBranchCorrect);

  // Notes on the sheet:
  //   Correct Take Branch
  //   Correct Prediction Branch Address
  //   Don't Care
  //   contents of rom_1 (hex, n*v repeats v):
  //   4*0 1 0 0 1 0 0 0 1 0 0 1 1 9*0 1 0 1
  //   contents of rom_2 (hex, n*v repeats v):
  //   0 0 0 60 60 0 5f 5f 5f 60 5 5 60 8 8 60 5f 8 8 60 5 7*60
  //   contents of rom_3 (hex, n*v repeats v):
  //   8*0 1 8*0 1
endmodule

module Counter (
  input  _1,
  input  _0,
  input  Enable,
  input  CountUp,
  input  CountDn,
  input  Clock,
  output OHalf
);

  wire comparator_1_eq, comparator_1_gt, controlled_buffer_1_out, or_1_out, or_3_out;
  wire [0:0] or_2_out;
  wire [1:0] counter_1_q;

  or or_1 (or_1_out, CountDn, _1, _0);
  or or_2 (or_2_out[0], _1, ~_0);  // OR_Gate
  or or_3 (or_3_out, CountDn, CountUp);
  Counter_part #(.width(2), .max('h3), .ongoal("stay")) counter_1 (
    .load(or_1_out), .D({1'b0, or_2_out[0]}), .count(or_3_out), .Q(counter_1_q), .clk(controlled_buffer_1_out));  // open: carry, clr
  assign controlled_buffer_1_out = Enable ? Clock : 1'bz;  // Controlled_Buffer controlled_buffer_1
  Comparator #(.width(2), .mode("unsigned")) comparator_1 (
    .a(counter_1_q), .b(2'b10), .gt(comparator_1_gt), .eq(comparator_1_eq));  // open: lt
  or or_4 (OHalf, comparator_1_gt, comparator_1_eq);

  // Other names for the same wires on the sheet: Dn = CountDn; Up = CountUp

  // Notes on the sheet:
  //   Reset when the Tag is wrong
endmodule
