// Logisim project SingleCycleMipsGiven.circ as structural Verilog: 10 circuits, main circuit main
module main (
);

  wire ALUSrc, and_1_out, and_2_out, Branch, Clock, Jal, Jr, Jump, MemRead, MemtoReg, MemWr, not_1_out,
       or_1_out, RegDst, RegWrite, Zero;
  wire [2:0] ALUOp;
  wire [4:0] Instr_20_16, Instr_25_21, WrAddr;
  wire [5:0] Instr_5_0, Instr_31_26;
  wire [15:6] Instr_15_0;
  wire [31:0] A, B, ImmValue, InstrOut, MemDataOut, multiplexer_6_out, PC, PCInc, Shifted, shifter_1_out,
       toJRMux, toJumpMux, toPC, WrData, WrtoReg, Z;

  Clock clock_1 (.out(Clock));
  PC pc_1 (.PCIn(toPC), .PCOut(PC), .Clock(Clock));
  PlusFourInc PCIncrement (.Input(PC), .Data_Out(PCInc));
  Register #(.width(32)) Instruction (
    .D(InstrOut), .Q({Instr_31_26, Instr_25_21, Instr_20_16, Instr_15_0, Instr_5_0}), .clk(Clock));  // open: en, clr
  Control_Unit control_unit_1 (
    .RegDst(RegDst), .RegWrite(RegWrite), .MemWr(MemWr), .MemtoReg(MemtoReg), .MemRead(MemRead),
    .Branch(Branch), .ALUOp(ALUOp), .in_1(Instr_31_26), .in_2(Instr_5_0), .ALUSrc(ALUSrc), .J(Jump), .Jr(Jr),
    .Jal(Jal));
  and and_1 (and_1_out, Branch, Zero);
  Multiplexer #(.width(32), .enable("false")) multiplexer_1 (
    .in0(PCInc), .in1(Shifted), .out(toJumpMux), .sel(and_1_out));
  // Probe on ALUOp
  Shifter #(.width(32)) shifter_1 (.in(ImmValue), .\dist (5'b00010), .out(shifter_1_out));
  Multiplexer #(.width(32), .enable("false")) multiplexer_2 (
    .in0(toJumpMux), .in1({PCInc[31:28], Instr_25_21, Instr_20_16, Instr_15_0, Instr_5_0, 2'b00}),
    .out(toJRMux), .sel(or_1_out));
  or or_1 (or_1_out, Jump, Jal);
  Multiplexer #(.select(2), .width(5), .enable("false")) multiplexer_3 (
    .in0(Instr_20_16), .in1(Instr_15_0[15:11]), .in2({5{1'b1}}), .in3({5{1'b1}}), .out(WrAddr),
    .sel({Jal, RegDst}));
  and and_2 (and_2_out, RegWrite, ~Clock);  // AND_Gate
  Multiplexer #(.width(32), .enable("false")) multiplexer_4 (.in0(Z), .in1(MemDataOut), .out(WrData), .sel(MemtoReg));
  Adder #(.width(32)) adder_1 (.a(PCInc), .b(shifter_1_out), .out(Shifted));  // open: cin, cout
  assign ImmValue = {{16{Instr_15_0[15]}}, {Instr_15_0, Instr_5_0}};  // Bit_Extender bit_extender_1
  RegFile regfile_1 (
    .WrAddr(WrAddr), .WrData(WrtoReg), .WrReg(and_2_out), .RdAddr1(Instr_25_21), .RdAddr2(Instr_20_16),
    .RdData1(A), .RdData2(B), .Clock(Clock));
  // Probe on A
  Multiplexer #(.width(32), .enable("false")) multiplexer_5 (.in0(WrData), .in1(PCInc), .out(WrtoReg), .sel(Jal));
  // Probe on B
  ALU alu_1 (
    .ALUCtl(ALUOp), .A(A), .B(multiplexer_6_out), .ALUResult(Z), .Zero(Zero), .Shamt({5{1'b0}}));  // open: Overflow
  Multiplexer #(.width(32), .enable("false")) multiplexer_6 (
    .in0(B), .in1(ImmValue), .out(multiplexer_6_out), .sel(ALUSrc));
  RAM RAM (.MemAddr(Z[7:0]), .MemDataIn(B), .Store(MemWr), .Clock(Clock), .Load(MemRead), .MemDataOut(MemDataOut));
  // Probe on Z
  not not_1 (not_1_out, Clock);
  Multiplexer #(.width(32), .enable("false")) multiplexer_7 (.in0(toJRMux), .in1(A), .out(toPC), .sel(Jr));
  ROM ROM (.ROM_Input(PC[9:2]), .ROM_Selector(not_1_out), .ROM_Output(InstrOut));
  // Probe on PC
  // Probe on Branch
  // Probe on Jump
  // Probe on Jal
  // Probe on Jr
  // Probe on RegWrite
  // Probe on WrAddr
  // Probe on WrtoReg
  // Probe on MemWr
  // Probe on B

  // Other names for the same wires on the sheet: Instr_15_0[5:0] = Instr_5_0; Instr_15_11[4:0] = Instr_15_0[15:11]
endmodule

module _32bit (
  input  Add_Sub_control,
  input  [31:0] in_2,
  input  [31:0] in_3,
  output [31:0] out_4,
  output carry_out
);

  wire adder_1_cout, subtractor_1_bout;
  wire [31:0] adder_1_out, subtractor_1_out;

  Adder #(.width(32)) adder_1 (.a(in_2), .b(in_3), .out(adder_1_out), .cout(adder_1_cout));  // open: cin
  Subtractor #(.width(32)) subtractor_1 (
    .a(in_2), .b(in_3), .out(subtractor_1_out), .bout(subtractor_1_bout));  // open: bin
  Multiplexer #(.width(32), .enable("false")) multiplexer_1 (
    .in0(adder_1_out), .in1(subtractor_1_out), .out(out_4), .sel(Add_Sub_control));
  Multiplexer #(.enable("false")) multiplexer_2 (
    .in0(adder_1_cout), .in1(subtractor_1_bout), .out(carry_out), .sel(Add_Sub_control));
endmodule

module ALU (
  input  [2:0] ALUCtl,
  input  [31:0] A,
  input  [31:0] B,
  input  [4:0] Shamt,
  output [31:0] ALUResult,
  output Zero,
  output Overflow
);

  wire and_2_out, and_3_out, comparator_1_lt, not_1_out, not_2_out, not_3_out, or_2_out;
  wire [31:0] Add, And, LessThan, Or, ShiftLeft, ShiftRight, Sub, Xor;

  Adder #(.width(32)) adder_1 (.a(A), .b(B), .out(Add));  // open: cin, cout
  Subtractor #(.width(32)) subtractor_1 (.a(A), .b(B), .out(Sub));  // open: bin, bout
  assign And = A & B;  // AND_Gate and_1, 32 bits wide
  assign Or = A | B;  // OR_Gate or_1, 32 bits wide
  assign Xor = A ^ B;  // XOR_Gate xor_1, 32 bits wide
  Comparator #(.width(32)) comparator_1 (.a(A), .b(B), .lt(comparator_1_lt));  // open: gt, eq
  assign LessThan = {{31{1'b0}}, comparator_1_lt};  // Bit_Extender bit_extender_1
  Shifter #(.width(32)) shifter_1 (.in(B), .\dist (Shamt), .out(ShiftLeft));
  Shifter #(.width(32), .shift("lr")) shifter_2 (.in(B), .\dist (Shamt), .out(ShiftRight));
  not not_1 (not_1_out, ALUCtl[0]);
  not not_2 (not_2_out, ALUCtl[1]);
  not not_3 (not_3_out, ALUCtl[2]);
  and and_2 (and_2_out, not_1_out, not_2_out, not_3_out);
  and and_3 (and_3_out, not_1_out, not_2_out, ALUCtl[2]);
  Multiplexer #(.select(3), .width(32), .enable("false")) multiplexer_1 (
    .in0(Sub), .in1(And), .in2(Add), .in3(Or), .in4(LessThan), .in5(Xor), .in6(ShiftLeft), .in7(ShiftRight),
    .out(ALUResult), .sel(ALUCtl));
  Overflow overflow_1 (
    .Add(and_2_out), .Sub(and_3_out), .ASign(A[31]), .BSign(B[31]), .ResultSign(ALUResult[31]),
    .Overflow(Overflow));
  not not_4 (Zero, or_2_out);
  or or_2 (or_2_out, ALUResult[0], ALUResult[1], ALUResult[2], ALUResult[3], ALUResult[4], ALUResult[5], ALUResult[6], ALUResult[7], ALUResult[8], ALUResult[9], ALUResult[10], ALUResult[11], ALUResult[12], ALUResult[13], ALUResult[14], ALUResult[15], ALUResult[16], ALUResult[17], ALUResult[18], ALUResult[19], ALUResult[20], ALUResult[21], ALUResult[22], ALUResult[23], ALUResult[24], ALUResult[25], ALUResult[26], ALUResult[27], ALUResult[28], ALUResult[29], ALUResult[30], ALUResult[31]);

  // Other names for the same wires on the sheet: ASign = A[31]; ResultSign = ALUResult[31]; BSign = B[31]
endmodule

module RegFile (
  input  [4:0] WrAddr,
  input  [31:0] WrData,
  input  WrReg,
  input  [4:0] RdAddr1,
  input  [4:0] RdAddr2,
  input  Clock,
  output [31:0] RdData1,
  output [31:0] RdData2
);

  wire WrReg0, WrReg1, WrReg2, WrReg3, WrReg4, WrReg5, WrReg6, WrReg7, WrReg8, WrReg9, WrReg10, WrReg11,
       WrReg12, WrReg13, WrReg14, WrReg15, WrReg16, WrReg17, WrReg18, WrReg19, WrReg20, WrReg21, WrReg22,
       WrReg23, WrReg24, WrReg25, WrReg26, WrReg27, WrReg28, WrReg29, WrReg30, WrReg31;
  wire [31:0] RegData1, RegData2, RegData3, RegData4, RegData5, RegData6, RegData7, RegData8, RegData9,
       RegData10, RegData11, RegData12, RegData13, RegData14, RegData15, RegData16, RegData17, RegData18,
       RegData19, RegData20, RegData21, RegData22, RegData23, RegData24, RegData25, RegData26, RegData27,
       RegData28, RegData29, RegData30, RegData31;

  Demultiplexer #(.select(5), .enable("false")) demultiplexer_1 (
    .out0(WrReg0), .out1(WrReg1), .out2(WrReg2), .out3(WrReg3), .out4(WrReg4), .out5(WrReg5), .out6(WrReg6),
    .out7(WrReg7), .out8(WrReg8), .out9(WrReg9), .out10(WrReg10), .out11(WrReg11), .out12(WrReg12),
    .out13(WrReg13), .out14(WrReg14), .out15(WrReg15), .out16(WrReg16), .out17(WrReg17), .out18(WrReg18),
    .out19(WrReg19), .out20(WrReg20), .out21(WrReg21), .out22(WrReg22), .out23(WrReg23), .out24(WrReg24),
    .out25(WrReg25), .out26(WrReg26), .out27(WrReg27), .out28(WrReg28), .out29(WrReg29), .out30(WrReg30),
    .out31(WrReg31), .in(WrReg), .sel(WrAddr));
  Register #(.width(32)) Reg4 (.D(WrData), .en(WrReg4), .Q(RegData4), .clk(Clock));  // open: clr
  Register #(.width(32)) Reg8 (.D(WrData), .en(WrReg8), .Q(RegData8), .clk(Clock));  // open: clr
  Register #(.width(32)) Reg12 (.D(WrData), .en(WrReg12), .Q(RegData12), .clk(Clock));  // open: clr
  Register #(.width(32)) Reg16 (.D(WrData), .en(WrReg16), .Q(RegData16), .clk(Clock));  // open: clr
  Register #(.width(32)) Reg20 (.D(WrData), .en(WrReg20), .Q(RegData20), .clk(Clock));  // open: clr
  Register #(.width(32)) Reg24 (.D(WrData), .en(WrReg24), .Q(RegData24), .clk(Clock));  // open: clr
  Register #(.width(32)) Reg28 (.D(WrData), .en(WrReg28), .Q(RegData28), .clk(Clock));  // open: clr
  Register #(.width(32)) Reg1 (.D(WrData), .en(WrReg1), .Q(RegData1), .clk(Clock));  // open: clr
  Register #(.width(32)) Reg5 (.D(WrData), .en(WrReg5), .Q(RegData5), .clk(Clock));  // open: clr
  Register #(.width(32)) Reg9 (.D(WrData), .en(WrReg9), .Q(RegData9), .clk(Clock));  // open: clr
  Register #(.width(32)) Reg13 (.D(WrData), .en(WrReg13), .Q(RegData13), .clk(Clock));  // open: clr
  Register #(.width(32)) Reg17 (.D(WrData), .en(WrReg17), .Q(RegData17), .clk(Clock));  // open: clr
  Register #(.width(32)) Reg21 (.D(WrData), .en(WrReg21), .Q(RegData21), .clk(Clock));  // open: clr
  Register #(.width(32)) Reg25 (.D(WrData), .en(WrReg25), .Q(RegData25), .clk(Clock));  // open: clr
  Register #(.width(32)) Reg29 (.D(WrData), .en(WrReg29), .Q(RegData29), .clk(Clock));  // open: clr
  Register #(.width(32)) Reg2 (.D(WrData), .en(WrReg2), .Q(RegData2), .clk(Clock));  // open: clr
  Register #(.width(32)) Reg6 (.D(WrData), .en(WrReg6), .Q(RegData6), .clk(Clock));  // open: clr
  Register #(.width(32)) Reg10 (.D(WrData), .en(WrReg10), .Q(RegData10), .clk(Clock));  // open: clr
  Register #(.width(32)) Reg14 (.D(WrData), .en(WrReg14), .Q(RegData14), .clk(Clock));  // open: clr
  Register #(.width(32)) Reg18 (.D(WrData), .en(WrReg18), .Q(RegData18), .clk(Clock));  // open: clr
  Register #(.width(32)) Reg22 (.D(WrData), .en(WrReg22), .Q(RegData22), .clk(Clock));  // open: clr
  Register #(.width(32)) Reg26 (.D(WrData), .en(WrReg26), .Q(RegData26), .clk(Clock));  // open: clr
  Register #(.width(32)) Reg30 (.D(WrData), .en(WrReg30), .Q(RegData30), .clk(Clock));  // open: clr
  Register #(.width(32)) Reg3 (.D(WrData), .en(WrReg3), .Q(RegData3), .clk(Clock));  // open: clr
  Register #(.width(32)) Reg7 (.D(WrData), .en(WrReg7), .Q(RegData7), .clk(Clock));  // open: clr
  Register #(.width(32)) Reg11 (.D(WrData), .en(WrReg11), .Q(RegData11), .clk(Clock));  // open: clr
  Register #(.width(32)) Reg15 (.D(WrData), .en(WrReg15), .Q(RegData15), .clk(Clock));  // open: clr
  Register #(.width(32)) Reg19 (.D(WrData), .en(WrReg19), .Q(RegData19), .clk(Clock));  // open: clr
  Register #(.width(32)) Reg23 (.D(WrData), .en(WrReg23), .Q(RegData23), .clk(Clock));  // open: clr
  Register #(.width(32)) Reg27 (.D(WrData), .en(WrReg27), .Q(RegData27), .clk(Clock));  // open: clr
  Register #(.width(32)) Reg31 (.D(WrData), .en(WrReg31), .Q(RegData31), .clk(Clock));  // open: clr
  Multiplexer #(.select(5), .width(32), .enable("false")) multiplexer_1 (
    .in0({32{1'b0}}), .in1(RegData1), .in2(RegData2), .in3(RegData3), .in4(RegData4), .in5(RegData5),
    .in6(RegData6), .in7(RegData7), .in8(RegData8), .in9(RegData9), .in10(RegData10), .in11(RegData11),
    .in12(RegData12), .in13(RegData13), .in14(RegData14), .in15(RegData15), .in16(RegData16),
    .in17(RegData17), .in18(RegData18), .in19(RegData19), .in20(RegData20), .in21(RegData21),
    .in22(RegData22), .in23(RegData23), .in24(RegData24), .in25(RegData25), .in26(RegData26),
    .in27(RegData27), .in28(RegData28), .in29(RegData29), .in30(RegData30), .in31(RegData31), .out(RdData1),
    .sel(RdAddr1));
  Multiplexer #(.select(5), .width(32), .enable("false")) multiplexer_2 (
    .in0({32{1'b0}}), .in1(RegData1), .in2(RegData2), .in3(RegData3), .in4(RegData4), .in5(RegData5),
    .in6(RegData6), .in7(RegData7), .in8(RegData8), .in9(RegData9), .in10(RegData10), .in11(RegData11),
    .in12(RegData12), .in13(RegData13), .in14(RegData14), .in15(RegData15), .in16(RegData16),
    .in17(RegData17), .in18(RegData18), .in19(RegData19), .in20(RegData20), .in21(RegData21),
    .in22(RegData22), .in23(RegData23), .in24(RegData24), .in25(RegData25), .in26(RegData26),
    .in27(RegData27), .in28(RegData28), .in29(RegData29), .in30(RegData30), .in31(RegData31), .out(RdData2),
    .sel(RdAddr2));
endmodule

module Overflow (
  input  Add,
  input  Sub,
  input  ASign,
  input  BSign,
  input  ResultSign,
  output Overflow
);

  wire and_1_out, and_2_out, or_1_out, xnor_1_out, xor_1_out, xor_2_out;

  xnor xnor_1 (xnor_1_out, ASign, BSign);
  xor xor_1 (xor_1_out, ASign, BSign);
  and and_1 (and_1_out, xnor_1_out, Add);
  and and_2 (and_2_out, xor_1_out, Sub);
  or or_1 (or_1_out, and_1_out, and_2_out);
  xor xor_2 (xor_2_out, ResultSign, ASign);
  and and_3 (Overflow, or_1_out, xor_2_out);

  // Notes on the sheet:
  //   Overflow occurs when doing addition and sign(A) == sign(B) && sign(result) != sign(A)
  //   Or
  //   Overflow occurs when doing subtraction and sign(A) != sign(B) && sign(result) != sign(A)
endmodule

module PlusFourInc (
  input  [31:0] Input,
  output [31:0] Data_Out
);

  Adder #(.width(32)) adder_1 (.a(Input), .b(32'h4), .out(Data_Out), .cin(1'b0));  // open: cout
endmodule

// Instruction Address (PC)
module PC (
  input  [31:0] PCIn,
  input  Clock,
  output [31:0] PCOut
);

  Register #(.width(32)) Instruction_Address__PC (.D(PCIn), .Q(PCOut), .clk(Clock));  // open: en, clr
endmodule

module ROM (
  input  [7:0] ROM_Input,
  input  ROM_Selector,
  output [31:0] ROM_Output
);

  ROM_part #(.dataWidth(32)) rom_1 (.addr(ROM_Input), .data(ROM_Output), .sel(ROM_Selector));

  // Notes on the sheet:
  //   ROM
  //   contents of rom_1 (hex, n*v repeats v):
  //   20010008 34220005 3043ffff 612020 832822 223024 c33825 aca40064 8ca80064 22482a 282a0005 11050003
  //   1034022 c00000b 200b0001 200c0005
endmodule

module RAM (
  input  [7:0] MemAddr,
  input  [31:0] MemDataIn,
  input  Store,
  input  Clock,
  input  Load,
  output [31:0] MemDataOut
);

  RAM_part #(.dataWidth(32), .bus("separate")) ram_1 (
    .addr(MemAddr), .din(MemDataIn), .data(MemDataOut), .str(Store), .sel(1'b1), .clk(Clock), .ld(Load),
    .clr(1'b0));
endmodule

module Control_Unit (
  input  [5:0] in_1,
  input  [5:0] in_2,
  output RegDst,
  output ALUSrc,
  output [2:0] ALUOp,
  output Branch,
  output MemWr,
  output MemRead,
  output MemtoReg,
  output RegWrite,
  output J,
  output Jr,
  output Jal
);

  wire and_2_out, and_3_out, and_5_out;
  wire [3:0] multiplexer_1_out;
  wire [4:4] or_1_out;

  Multiplexer #(.width(4), .enable("false")) multiplexer_1 (
    .in0(in_1[3:0]), .in1(in_2[3:0]), .out(multiplexer_1_out), .sel(RegDst));
  and and_1 (MemWr, in_1[0], in_1[1], ~in_1[2], in_1[3], ~in_1[4], in_1[5]);  // AND_Gate
  and and_2 (and_2_out, ~in_1[0], ~in_1[1], in_1[2], ~in_1[3], ~in_1[4], ~in_1[5]);  // AND_Gate
  and and_3 (and_3_out, ~in_1[0], in_1[1], ~in_1[2], ~in_1[3], ~in_1[4], ~in_1[5]);  // AND_Gate
  or or_1 (or_1_out[4], Branch, J);
  and and_4 (RegWrite, ~MemWr, ~and_2_out, ~and_3_out, ~Jr);  // AND_Gate
  and and_5 (and_5_out, ~in_2[0], ~in_2[1], ~in_2[2], in_2[3], ~in_2[4], ~in_2[5]);  // AND_Gate
  and and_6 (J, ~in_1[0], in_1[1], ~in_1[2], ~in_1[3], ~in_1[4], ~in_1[5]);  // AND_Gate
  and and_7 (Jr, RegDst, and_5_out);
  and and_8 (Jal, in_1[0], in_1[1], ~in_1[2], ~in_1[3], ~in_1[4], ~in_1[5]);  // AND_Gate
  and and_9 (RegDst, ~in_1[0], ~in_1[1], ~in_1[2], ~in_1[3], ~in_1[4], ~in_1[5]);  // AND_Gate
  ROM_part #(.addrWidth(5), .dataWidth(3)) rom_1 (.addr({or_1_out[4], multiplexer_1_out}), .data(ALUOp));  // open: sel
  and and_10 (Branch, ~in_1[0], ~in_1[1], in_1[2], ~in_1[3], ~in_1[4], ~in_1[5]);  // AND_Gate
  and and_11 (MemRead, in_1[0], in_1[1], ~in_1[2], ~in_1[3], ~in_1[4], in_1[5]);  // AND_Gate
  and and_12 (ALUSrc, ~RegDst, ~Branch);  // AND_Gate

  assign MemtoReg = MemRead;

  // Other names for the same wires on the sheet: AluOp_t = RegDst; funct[5:0] = in_2; Jump = J; Opcode[5:0] = in_1

  // Notes on the sheet:
  //   contents of rom_1 (hex, n*v repeats v):
  //   2 0 0 2 1 3 0 0 2 0 4 2 1 3 0 0 16*2
endmodule
