// Logisim project 154blab1part1.circ as structural Verilog: 10 circuits, main circuit m1out1
module m1out1 (
  input  In7,
  input  In6,
  input  In5,
  input  In4,
  input  In3,
  input  In2,
  input  In1,
  input  In0,
  output Out2,
  output Out1,
  output Out0
);

  wire and_1_out, and_2_out, not_1_out;

  not not_1 (not_1_out, In1);
  and and_1 (and_1_out, In2, not_1_out);
  and and_2 (and_2_out, not_1_out, In0);
  or or_1 (Out1, and_1_out, and_2_out);
endmodule

module m1out2 (
  input  In7,
  input  In6,
  input  In5,
  input  In4,
  input  In3,
  input  In2,
  input  In1,
  input  In0,
  output Out2,
  output Out1,
  output Out0
);

  wire and_1_out, and_2_out, and_3_out, not_1_out, not_2_out;

  and and_1 (and_1_out, In2, In1);
  not not_1 (not_1_out, In0);
  and and_2 (and_2_out, In2, not_1_out);
  not not_2 (not_2_out, In2);
  and and_3 (and_3_out, not_2_out, In0);
  or or_1 (Out2, In3, and_1_out, and_2_out, and_3_out);
endmodule

module m1out0 (
  input  In7,
  input  In6,
  input  In5,
  input  In4,
  input  In3,
  input  In2,
  input  In1,
  input  In0,
  output Out2,
  output Out1,
  output Out0
);

  wire and_1_out, and_2_out, not_1_out, not_2_out;

  not not_1 (not_1_out, In1);
  and and_1 (and_1_out, not_1_out, In0);
  and and_2 (and_2_out, In1, not_2_out);
  not not_2 (not_2_out, In0);
  or or_1 (Out0, In3, and_1_out, and_2_out);
endmodule

module m0out1 (
  input  In7,
  input  In6,
  input  In5,
  input  In4,
  input  In3,
  input  In2,
  input  In1,
  input  In0,
  output Out2,
  output Out1,
  output Out0
);

  and and_1 (Out1, In7, In6);
endmodule

module m0out0 (
  input  In7,
  input  In6,
  input  In5,
  input  In4,
  input  In3,
  input  In2,
  input  In1,
  input  In0,
  output Out2,
  output Out1,
  output Out0
);

  wire and_1_out, and_2_out, not_1_out, not_2_out;

  not not_1 (not_1_out, In7);
  not not_2 (not_2_out, In5);
  and and_1 (and_1_out, not_1_out, not_2_out);
  and and_2 (and_2_out, In6, In4);
  or or_1 (Out0, and_1_out, and_2_out);
endmodule

module m0 (
  input  In7,
  input  In6,
  input  In5,
  input  In4,
  input  In3,
  input  In2,
  input  In1,
  input  In0,
  output Out2,
  output Out1,
  output Out0
);

  m0out1 m0out1_1 (.In7(In7), .In6(In6), .Out1(Out1));  // open: In5, In4, In3, In2, In1, In0, Out2, Out0
  m0out0 u_Out0 (.In7(In7), .In6(In6), .In5(In5), .In4(In4), .Out0(Out0));  // open: In3, In2, In1, In0, Out2, Out1

  assign Out2 = 1'b0;
endmodule

module m1 (
  input  In7,
  input  In6,
  input  In5,
  input  In4,
  input  In3,
  input  In2,
  input  In1,
  input  In0,
  output Out2,
  output Out1,
  output Out0
);

  m1out2 u_Out2 (.In3(In3), .In2(In2), .In1(In1), .In0(In0), .Out2(Out2));  // open: In7, In6, In5, In4, Out1, Out0
  m1out1 u_Out1 (.In2(In2), .In1(In1), .In0(In0), .Out1(Out1));  // open: In7, In6, In5, In4, In3, Out2, Out0
  m1out0 u_Out0 (.In3(In3), .In1(In1), .In0(In0), .Out0(Out0));  // open: In7, In6, In5, In4, In2, Out2, Out1
endmodule

module part1template (
  input  In7,
  input  In6,
  input  In5,
  input  In4,
  input  In3,
  input  In2,
  input  In1,
  input  In0,
  output Out2,
  output Out1,
  output Out0
);
endmodule

module part1comb (
  input  [7:0] in_1,
  output Out2,
  output Out1,
  output Out0
);

  wire and_1_out, and_2_out, and_3_out, and_4_out, and_5_out, and_6_out, and_7_out, m0_1_out0, m0_1_out1,
       m0_1_out2, m1_1_out0, m1_1_out1, m1_1_out2, or_1_out;

  m1 m1_1 (
    .In3(in_1[3]), .In2(in_1[2]), .In1(in_1[1]), .In0(in_1[0]), .Out2(m1_1_out2), .Out1(m1_1_out1),
    .Out0(m1_1_out0));  // open: In7, In6, In5, In4
  m0 m0_1 (
    .In7(in_1[7]), .In6(in_1[6]), .In5(in_1[5]), .In4(in_1[4]), .Out2(m0_1_out2), .Out1(m0_1_out1),
    .Out0(m0_1_out0));  // open: In3, In2, In1, In0
  and and_1 (and_1_out, ~in_1[4], ~in_1[5], ~in_1[6], ~in_1[7]);  // AND_Gate
  or or_1 (or_1_out, in_1[4], in_1[5], in_1[6], in_1[7]);
  and and_2 (and_2_out, and_1_out, m1_1_out2);
  and and_3 (and_3_out, and_1_out, m1_1_out1);
  and and_4 (and_4_out, m0_1_out2, or_1_out);
  and and_5 (and_5_out, m0_1_out1, or_1_out);
  and and_6 (and_6_out, m0_1_out0, or_1_out);
  and and_7 (and_7_out, and_1_out, m1_1_out0);
  or or_2 (Out2, and_2_out, and_4_out);
  or or_3 (Out1, and_3_out, and_5_out);
  or or_4 (Out0, and_7_out, and_6_out);
endmodule

module part1ROM (
  input  [7:0] in_1,
  output Out2,
  output Out1,
  output Out0
);

  ROM #(.dataWidth(3)) rom_1 (.addr(in_1), .data({Out2, Out1, Out0}));  // open: sel

  // Notes on the sheet:
  //   contents of rom_1 (hex, n*v repeats v):
  //   0 7 1 0 6 3 0 4 0 0 5 53*0 16*1 112*0 16*2 16*3
endmodule
