// Logisim project 154bpart2.circ as structural Verilog: 1 circuit, main circuit main
module main (
  input  In,
  input  Select,
  input  Clock,
  output Out
);

  wire [3:0] register_1_q;
  wire [4:0] rom_1_data;
  wire [4:4] register_1_q_2;

  ROM #(.addrWidth(5), .dataWidth(5)) rom_1 (.addr({In, register_1_q}), .data(rom_1_data), .sel(Select));
  Register #(.width(5)) register_1 (
    .D(rom_1_data), .Q({register_1_q_2[4], register_1_q}), .clk(Clock));  // open: en, clr
  Register #(.width(1)) register_2 (.D(register_1_q_2[4]), .Q(Out), .clk(Clock));  // open: en, clr

  // Notes on the sheet:
  //   contents of rom_1 (hex, n*v repeats v):
  //   1 3 4 6 6 7 9 9 a 0 10 5*0 2 4 5 6 7 8 9 a a 10 10
endmodule
