// Logisim project MultiCycleMipsGiven.circ as structural Verilog: 6 circuits, main circuit main
module main (
);

  wire ALUshamtEn, ALUSrcA, and_1_out, Clock, IorD, IRWrite, MemRead, MemWrite, or_1_out, PCWrite,
       PCWriteCond, RegWrite, Zero;
  wire [1:0] ALUSrcB, MemtoReg, PCSource, RegDst;
  wire [2:0] ALUOp;
  wire [4:0] controlled_buffer_1_out, D_reg, WrAddr;
  wire [5:0] funct;
  wire [7:0] multiplexer_3_out;
  wire [31:0] A, ALUout, ALUResult, B, immediate, immshift, MD, MDR, multiplexer_4_out, multiplexer_5_out,
       nPC, PC, regfile_1_rddata1, regfile_1_rddata2, WrData;
  wire [31:6] IR;

  Clock clock_1 (.out(Clock));
  or or_1 (or_1_out, and_1_out, PCWrite);
  and and_1 (and_1_out, Zero, PCWriteCond);
  Multiplexer #(.select(2), .width(5), .enable("false")) multiplexer_1 (
    .in0(D_reg), .in1(IR[20:16]), .in2({5{1'b1}}), .out(WrAddr), .sel(RegDst));  // open: in3
  Register #(.width(32)) u_PC (.D(nPC), .en(or_1_out), .Q(PC), .clk(Clock));  // open: clr
  Multiplexer #(.select(2), .width(32), .enable("false")) multiplexer_2 (
    .in0(ALUout), .in1(MDR), .in2(PC), .out(WrData), .sel(MemtoReg));  // open: in3
  RegFile regfile_1 (
    .WrAddr(WrAddr), .WrData(WrData), .WrReg(RegWrite), .RdAddr1(IR[25:21]), .RdAddr2(IR[20:16]),
    .RdData1(regfile_1_rddata1), .RdData2(regfile_1_rddata2), .Clock(Clock));
  Multiplexer #(.width(8), .enable("false")) multiplexer_3 (
    .in0(PC[9:2]), .in1(ALUout[9:2]), .out(multiplexer_3_out), .sel(IorD));
  Register #(.width(32)) u_MDR (.D(MD), .Q(MDR), .clk(Clock));  // open: en, clr
  Register #(.width(32)) u_A (.D(regfile_1_rddata1), .Q(A), .clk(Clock));  // open: en, clr
  Register #(.width(32)) u_B (.D(regfile_1_rddata2), .Q(B), .clk(Clock));  // open: en, clr
  RAM #(.dataWidth(32), .bus("separate")) ram_1 (
    .addr(multiplexer_3_out), .din(B), .data(MD), .str(MemWrite), .sel(1'b1), .clk(Clock), .ld(MemRead));  // open: clr
  Register #(.width(32)) u_IR (
    .D(MD), .en(IRWrite), .Q({IR[31:16], D_reg, IR[10:6], funct}), .clk(Clock));  // open: clr
  Multiplexer #(.select(2), .width(32), .enable("false")) multiplexer_4 (
    .in0(B), .in1(32'h4), .in2(immediate), .in3(immshift), .out(multiplexer_4_out), .sel(ALUSrcB));
  ALU alu_1 (
    .ALUCtl(ALUOp), .A(multiplexer_5_out), .B(multiplexer_4_out), .ALUResult(ALUResult), .Zero(Zero),
    .Shamt(controlled_buffer_1_out));  // open: Overflow
  Multiplexer #(.width(32), .enable("false")) multiplexer_5 (.in0(PC), .in1(A), .out(multiplexer_5_out), .sel(ALUSrcA));
  assign controlled_buffer_1_out = ALUshamtEn ? IR[10:6] : 5'bz;  // Controlled_Buffer controlled_buffer_1
  assign immediate = {{16{D_reg[4]}}, {D_reg, IR[10:6], funct}};  // Bit_Extender bit_extender_1
  Shifter #(.width(32)) shifter_1 (.in(immediate), .\dist (5'b00010), .out(immshift));
  Register #(.width(32)) u_ALUout (.D(ALUResult), .Q(ALUout), .clk(Clock));  // open: en, clr
  microcontrol microcontrol_1 (
    .Clock(Clock), .Opcode(IR[31:26]), .Funct(funct), .MemRead(MemRead), .MemWrite(MemWrite),
    .ALUshamtEn(ALUshamtEn), .ALUSrcB(ALUSrcB), .ALUSrcA(ALUSrcA), .RegWrite(RegWrite), .RegDst(RegDst),
    .ALUOp(ALUOp), .PCWriteCond(PCWriteCond), .PCWrite(PCWrite), .IorD(IorD), .IRWrite(IRWrite),
    .PCSource(PCSource), .MemtoReg(MemtoReg));
  Multiplexer #(.select(2), .width(32), .enable("false")) multiplexer_6 (
    .in0(ALUResult), .in1(ALUout), .in2({PC[31:28], IR[25:16], D_reg, IR[10:6], funct, 2'b00}), .in3(A),
    .out(nPC), .sel(PCSource));
  // Probe on PC
  // Probe on PCWriteCond
  // Probe on RegWrite
  // Probe on WrAddr
  // Probe on WrData
  // Probe on MemWrite
  // Probe on B

  // Other names for the same wires on the sheet: opcode[5:0] = IR[31:26]; IR (some bits) = {D_reg, funct};
  //   PC_shifted[31:2] = {PC[31:28], IR[25:16], D_reg, IR[10:6], funct}; shamt[4:0] = IR[10:6];
  //   T_reg[4:0] = IR[20:16]; S_reg[4:0] = IR[25:21]; PC_top[3:0] = PC[31:28]

  // Notes on the sheet:
  //   RAM
  //   R-type split
  //   I-type
  //   J-type
endmodule

module _32bit (
  input  Add_Sub_control,
  input  [31:0] in_2,
  input  [31:0] in_3,
  output [31:0] out_4,
  output carry_out
);

  wire adder_1_cout, subtractor_1_bout;
  wire [31:0] adder_1_out, subtractor_1_out;

  Adder #(.width(32)) adder_1 (.a(in_2), .b(in_3), .out(adder_1_out), .cout(adder_1_cout));  // open: cin
  Subtractor #(.width(32)) subtractor_1 (
    .a(in_2), .b(in_3), .out(subtractor_1_out), .bout(subtractor_1_bout));  // open: bin
  Multiplexer #(.width(32), .enable("false")) multiplexer_1 (
    .in0(adder_1_out), .in1(subtractor_1_out), .out(out_4), .sel(Add_Sub_control));
  Multiplexer #(.enable("false")) multiplexer_2 (
    .in0(adder_1_cout), .in1(subtractor_1_bout), .out(carry_out), .sel(Add_Sub_control));
endmodule

module ALU (
  input  [2:0] ALUCtl,
  input  [31:0] A,
  input  [31:0] B,
  input  [4:0] Shamt,
  output [31:0] ALUResult,
  output Zero,
  output Overflow
);

  wire and_2_out, and_3_out, comparator_1_lt, not_1_out, not_2_out, not_3_out, not_4_out, not_5_out, or_2_out;
  wire [31:0] Add, And, LessThan, Nor, Or, ShiftLeft, ShiftRight, Sub, Xor;

  Adder #(.width(32)) adder_1 (.a(A), .b(B), .out(Add));  // open: cin, cout
  Subtractor #(.width(32)) subtractor_1 (.a(A), .b(B), .out(Sub));  // open: bin, bout
  assign And = A & B;  // AND_Gate and_1, 32 bits wide
  assign Or = A | B;  // OR_Gate or_1, 32 bits wide
  assign Nor = ~(A | B);  // NOR_Gate nor_1, 32 bits wide
  Comparator #(.width(32)) comparator_1 (.a(A), .b(B), .lt(comparator_1_lt));  // open: gt, eq
  assign LessThan = {{31{1'b0}}, comparator_1_lt};  // Bit_Extender bit_extender_1
  Shifter #(.width(32)) shifter_1 (.in(B), .\dist (Shamt), .out(ShiftLeft));
  Shifter #(.width(32), .shift("lr")) shifter_2 (.in(B), .\dist (Shamt), .out(ShiftRight));
  not not_1 (not_1_out, ALUCtl[0]);
  not not_2 (not_2_out, ALUCtl[1]);
  not not_3 (not_3_out, ALUCtl[2]);
  not not_4 (not_4_out, ALUCtl[0]);
  not not_5 (not_5_out, ALUCtl[2]);
  and and_2 (and_2_out, not_1_out, not_2_out, not_3_out);
  and and_3 (and_3_out, not_4_out, ALUCtl[1], not_5_out);
  Multiplexer #(.select(3), .width(32), .enable("false")) multiplexer_1 (
    .in0(Sub), .in1(And), .in2(Add), .in3(Or), .in4(LessThan), .in5(ShiftLeft), .in6(ShiftRight), .in7(Xor),
    .out(ALUResult), .sel(ALUCtl));
  Overflow overflow_1 (
    .Add(and_3_out), .Sub(and_2_out), .ASign(A[31]), .BSign(B[31]), .ResultSign(ALUResult[31]),
    .Overflow(Overflow));
  or or_2 (or_2_out, ALUResult[0], ALUResult[1], ALUResult[2], ALUResult[3], ALUResult[4], ALUResult[5], ALUResult[6], ALUResult[7], ALUResult[8], ALUResult[9], ALUResult[10], ALUResult[11], ALUResult[12], ALUResult[13], ALUResult[14], ALUResult[15], ALUResult[16], ALUResult[17], ALUResult[18], ALUResult[19], ALUResult[20], ALUResult[21], ALUResult[22], ALUResult[23], ALUResult[24], ALUResult[25], ALUResult[26], ALUResult[27], ALUResult[28], ALUResult[29], ALUResult[30], ALUResult[31]);
  not not_6 (Zero, or_2_out);

  // Other names for the same wires on the sheet: ASign = A[31]; ResultSign = ALUResult[31]; BSign = B[31]
endmodule

module RegFile (
  input  [4:0] WrAddr,
  input  [31:0] WrData,
  input  WrReg,
  input  [4:0] RdAddr1,
  input  [4:0] RdAddr2,
  input  Clock,
  output [31:0] RdData1,
  output [31:0] RdData2
);

  wire WrReg0, WrReg1, WrReg2, WrReg3, WrReg4, WrReg5, WrReg6, WrReg7, WrReg8, WrReg9, WrReg10, WrReg11,
       WrReg12, WrReg13, WrReg14, WrReg15, WrReg16, WrReg17, WrReg18, WrReg19, WrReg20, WrReg21, WrReg22,
       WrReg23, WrReg24, WrReg25, WrReg26, WrReg27, WrReg28, WrReg29, WrReg30, WrReg31;
  wire [31:0] RegData1, RegData2, RegData3, RegData4, RegData5, RegData6, RegData7, RegData8, RegData9,
       RegData10, RegData11, RegData12, RegData13, RegData14, RegData15, RegData16, RegData17, RegData18,
       RegData19, RegData20, RegData21, RegData22, RegData23, RegData24, RegData25, RegData26, RegData27,
       RegData28, RegData29, RegData30, RegData31;

  Demultiplexer #(.select(5), .enable("false")) demultiplexer_1 (
    .out0(WrReg0), .out1(WrReg1), .out2(WrReg2), .out3(WrReg3), .out4(WrReg4), .out5(WrReg5), .out6(WrReg6),
    .out7(WrReg7), .out8(WrReg8), .out9(WrReg9), .out10(WrReg10), .out11(WrReg11), .out12(WrReg12),
    .out13(WrReg13), .out14(WrReg14), .out15(WrReg15), .out16(WrReg16), .out17(WrReg17), .out18(WrReg18),
    .out19(WrReg19), .out20(WrReg20), .out21(WrReg21), .out22(WrReg22), .out23(WrReg23), .out24(WrReg24),
    .out25(WrReg25), .out26(WrReg26), .out27(WrReg27), .out28(WrReg28), .out29(WrReg29), .out30(WrReg30),
    .out31(WrReg31), .in(WrReg), .sel(WrAddr));
  Register #(.width(32)) Reg4 (.D(WrData), .en(WrReg4), .Q(RegData4), .clk(Clock));  // open: clr
  Register #(.width(32)) Reg8 (.D(WrData), .en(WrReg8), .Q(RegData8), .clk(Clock));  // open: clr
  Register #(.width(32)) Reg12 (.D(WrData), .en(WrReg12), .Q(RegData12), .clk(Clock));  // open: clr
  Register #(.width(32)) Reg16 (.D(WrData), .en(WrReg16), .Q(RegData16), .clk(Clock));  // open: clr
  Register #(.width(32)) Reg20 (.D(WrData), .en(WrReg20), .Q(RegData20), .clk(Clock));  // open: clr
  Register #(.width(32)) Reg24 (.D(WrData), .en(WrReg24), .Q(RegData24), .clk(Clock));  // open: clr
  Register #(.width(32)) Reg28 (.D(WrData), .en(WrReg28), .Q(RegData28), .clk(Clock));  // open: clr
  Register #(.width(32)) Reg1 (.D(WrData), .en(WrReg1), .Q(RegData1), .clk(Clock));  // open: clr
  Register #(.width(32)) Reg5 (.D(WrData), .en(WrReg5), .Q(RegData5), .clk(Clock));  // open: clr
  Register #(.width(32)) Reg9 (.D(WrData), .en(WrReg9), .Q(RegData9), .clk(Clock));  // open: clr
  Register #(.width(32)) Reg13 (.D(WrData), .en(WrReg13), .Q(RegData13), .clk(Clock));  // open: clr
  Register #(.width(32)) Reg17 (.D(WrData), .en(WrReg17), .Q(RegData17), .clk(Clock));  // open: clr
  Register #(.width(32)) Reg21 (.D(WrData), .en(WrReg21), .Q(RegData21), .clk(Clock));  // open: clr
  Register #(.width(32)) Reg25 (.D(WrData), .en(WrReg25), .Q(RegData25), .clk(Clock));  // open: clr
  Register #(.width(32)) Reg29 (.D(WrData), .en(WrReg29), .Q(RegData29), .clk(Clock));  // open: clr
  Register #(.width(32)) Reg2 (.D(WrData), .en(WrReg2), .Q(RegData2), .clk(Clock));  // open: clr
  Register #(.width(32)) Reg6 (.D(WrData), .en(WrReg6), .Q(RegData6), .clk(Clock));  // open: clr
  Register #(.width(32)) Reg10 (.D(WrData), .en(WrReg10), .Q(RegData10), .clk(Clock));  // open: clr
  Register #(.width(32)) Reg14 (.D(WrData), .en(WrReg14), .Q(RegData14), .clk(Clock));  // open: clr
  Register #(.width(32)) Reg18 (.D(WrData), .en(WrReg18), .Q(RegData18), .clk(Clock));  // open: clr
  Register #(.width(32)) Reg22 (.D(WrData), .en(WrReg22), .Q(RegData22), .clk(Clock));  // open: clr
  Register #(.width(32)) Reg26 (.D(WrData), .en(WrReg26), .Q(RegData26), .clk(Clock));  // open: clr
  Register #(.width(32)) Reg30 (.D(WrData), .en(WrReg30), .Q(RegData30), .clk(Clock));  // open: clr
  Register #(.width(32)) Reg3 (.D(WrData), .en(WrReg3), .Q(RegData3), .clk(Clock));  // open: clr
  Register #(.width(32)) Reg7 (.D(WrData), .en(WrReg7), .Q(RegData7), .clk(Clock));  // open: clr
  Register #(.width(32)) Reg11 (.D(WrData), .en(WrReg11), .Q(RegData11), .clk(Clock));  // open: clr
  Register #(.width(32)) Reg15 (.D(WrData), .en(WrReg15), .Q(RegData15), .clk(Clock));  // open: clr
  Register #(.width(32)) Reg19 (.D(WrData), .en(WrReg19), .Q(RegData19), .clk(Clock));  // open: clr
  Register #(.width(32)) Reg23 (.D(WrData), .en(WrReg23), .Q(RegData23), .clk(Clock));  // open: clr
  Register #(.width(32)) Reg27 (.D(WrData), .en(WrReg27), .Q(RegData27), .clk(Clock));  // open: clr
  Register #(.width(32)) Reg31 (.D(WrData), .en(WrReg31), .Q(RegData31), .clk(Clock));  // open: clr
  Multiplexer #(.select(5), .width(32), .enable("false")) multiplexer_1 (
    .in0({32{1'b0}}), .in1(RegData1), .in2(RegData2), .in3(RegData3), .in4(RegData4), .in5(RegData5),
    .in6(RegData6), .in7(RegData7), .in8(RegData8), .in9(RegData9), .in10(RegData10), .in11(RegData11),
    .in12(RegData12), .in13(RegData13), .in14(RegData14), .in15(RegData15), .in16(RegData16),
    .in17(RegData17), .in18(RegData18), .in19(RegData19), .in20(RegData20), .in21(RegData21),
    .in22(RegData22), .in23(RegData23), .in24(RegData24), .in25(RegData25), .in26(RegData26),
    .in27(RegData27), .in28(RegData28), .in29(RegData29), .in30(RegData30), .in31(RegData31), .out(RdData1),
    .sel(RdAddr1));
  Multiplexer #(.select(5), .width(32), .enable("false")) multiplexer_2 (
    .in0({32{1'b0}}), .in1(RegData1), .in2(RegData2), .in3(RegData3), .in4(RegData4), .in5(RegData5),
    .in6(RegData6), .in7(RegData7), .in8(RegData8), .in9(RegData9), .in10(RegData10), .in11(RegData11),
    .in12(RegData12), .in13(RegData13), .in14(RegData14), .in15(RegData15), .in16(RegData16),
    .in17(RegData17), .in18(RegData18), .in19(RegData19), .in20(RegData20), .in21(RegData21),
    .in22(RegData22), .in23(RegData23), .in24(RegData24), .in25(RegData25), .in26(RegData26),
    .in27(RegData27), .in28(RegData28), .in29(RegData29), .in30(RegData30), .in31(RegData31), .out(RdData2),
    .sel(RdAddr2));
endmodule

module Overflow (
  input  Add,
  input  Sub,
  input  ASign,
  input  BSign,
  input  ResultSign,
  output Overflow
);

  wire and_1_out, and_2_out, or_1_out, xnor_1_out, xor_1_out, xor_2_out;

  xnor xnor_1 (xnor_1_out, ASign, BSign);
  xor xor_1 (xor_1_out, ASign, BSign);
  and and_1 (and_1_out, xnor_1_out, Add);
  and and_2 (and_2_out, xor_1_out, Sub);
  or or_1 (or_1_out, and_1_out, and_2_out);
  xor xor_2 (xor_2_out, ResultSign, ASign);
  and and_3 (Overflow, or_1_out, xor_2_out);

  // Notes on the sheet:
  //   Overflow occurs when doing addition and sign(A) == sign(B) && sign(result) != sign(A)
  //   Or
  //   Overflow occurs when doing subtraction and sign(A) != sign(B) && sign(result) != sign(A)
endmodule

module microcontrol (
  input  Clock,
  input  [5:0] Funct,
  input  [5:0] Opcode,
  output [1:0] PCSource,
  output PCWriteCond,
  output PCWrite,
  output IorD,
  output IRWrite,
  output [1:0] MemtoReg,
  output MemRead,
  output MemWrite,
  output ALUshamtEn,
  output [1:0] ALUSrcB,
  output ALUSrcA,
  output RegWrite,
  output [1:0] RegDst,
  output [2:0] ALUOp
);

  wire [3:0] Next_State;
  wire [23:20] rom_1_data;

  ROM #(.addrWidth(16), .dataWidth(24)) rom_1 (
    .addr({Opcode, Funct, Next_State}),
    .data({rom_1_data, ALUOp, RegDst, RegWrite, ALUSrcA, ALUSrcB, ALUshamtEn, MemWrite, MemRead, MemtoReg, IRWrite, IorD, PCWrite, PCWriteCond, PCSource}));  // open: sel
  Register #(.width(4)) register_1 (.D(rom_1_data), .Q(Next_State), .clk(Clock));  // open: en, clr

  // Notes on the sheet:
  //   contents of rom_1 (hex, n*v repeats v):
  //   140928 841800 a b 1408a 1804 d03000 ca2000 ca0400 43000 e00110 210 4000 c000 c040 0 140928 741800 a
  //   b 1408a 1804 d03000 c02000 c00400 43000 e00110 210 4000 c000 c040 0 140928 841800 a b 1408a 1804
  //   d03000 cc2000 cc0400 43000 e00110 210 4000 c000 c040 0 140928 741800 a b 1408a 1804 d03000 c02000
  //   c00400 43000 e00110 210 4000 c000 c040 0 140928 741800 a b 1408a 1804 d03000 c02000 c00400 43000
  //   e00110 210 4000 c000 c040 0 140928 741800 a b 1408a 1804 d03000 c02000 c00400 43000 e00110 210 4000
  //   c000 c040 0 140928 741800 a b 1408a 1804 d03000 c02000 c00400 43000 e00110 210 4000 c000 c040 0
  //   140928 741800 a b 1408a 1804 d03000 c02000 c00400 43000 e00110 210 4000 c000 c040 0 140928 341800 a
  //   b 1408a 1804 d03000 c02000 c00400 43000 e00110 210 4000 c000 c040 0 140928 741800 a b 1408a 1804
  //   d03000 c02000 c00400 43000 e00110 210 4000 c000 c040 0 140928 741800 a b 1408a 1804 d03000 c02000
  //   c00400 43000 e00110 210 4000 c000 c040 0 140928 741800 a b 1408a 1804 d03000 c02000 c00400 43000
  //   e00110 210 4000 c000 c040 0 140928 741800 a b 1408a 1804 d03000 c02000 c00400 43000 e00110 210 4000
  //   c000 c040 0 140928 741800 a b 1408a 1804 d03000 c02000 c00400 43000 e00110 210 4000 c000 c040 0
  //   140928 741800 a b 1408a 1804 d03000 c02000 c00400 43000 e00110 210 4000 c000 c040 0 140928 741800 a
  //   b 1408a 1804 d03000 c02000 c00400 43000 e00110 210 4000 c000 c040 0 140928 741800 a b 1408a 1804
  //   d03000 c02000 c00400 43000 e00110 210 4000 c000 c040 0 140928 741800 a b 1408a 1804 d03000 c02000
  //   c00400 43000 e00110 210 4000 c000 c040 0 140928 741800 a b 1408a 1804 d03000 c02000 c00400 43000
  //   e00110 210 4000 c000 c040 0 140928 741800 a b 1408a 1804 d03000 c02000 c00400 43000 e00110 210 4000
  //   c000 c040 0 140928 741800 a b 1408a 1804 d03000 c02000 c00400 43000 e00110 210 4000 c000 c040 0
  //   140928 741800 a b 1408a 1804 d03000 c02000 c00400 43000 e00110 210 4000 c000 c040 0 140928 741800 a
  //   b 1408a 1804 d03000 c02000 c00400 43000 e00110 210 4000 c000 c040 0 140928 741800 a b 1408a 1804
  //   d03000 c02000 c00400 43000 e00110 210 4000 c000 c040 0 140928 741800 a b 1408a 1804 d03000 c02000
  //   c00400 43000 e00110 210 4000 c000 c040 0 140928 741800 a b 1408a 1804 d03000 c02000 c00400 43000
  //   e00110 210 4000 c000 c040 0 140928 741800 a b 1408a 1804 d03000 c02000 c00400 43000 e00110 210 4000
  //   c000 c040 0 140928 741800 a b 1408a 1804 d03000 c02000 c00400 43000 e00110 210 4000 c000 c040 0
  //   140928 741800 a b 1408a 1804 d03000 c02000 c00400 43000 e00110 210 4000 c000 c040 0 140928 741800 a
  //   b 1408a 1804 d03000 c02000 c00400 43000 e00110 210 4000 c000 c040 0 140928 741800 a b 1408a 1804
  //   d03000 c02000 c00400 43000 e00110 210 4000 c000 c040 0 140928 741800 a b 1408a 1804 d03000 c02000
  //   c00400 43000 e00110 210 4000 c000 c040 0 140928 741800 a b 1408a 1804 d03000 c42000 c00400 43000
  //   e00110 210 4000 c000 c040 0 140928 741800 a b 1408a 1804 d03000 c02000 c00400 43000 e00110 210 4000
  //   c000 c040 0 140928 741800 a b 1408a 1804 d03000 c02000 c00400 43000 e00110 210 4000 c000 c040 0
  //   140928 741800 a b 1408a 1804 d03000 c02000 c00400 43000 e00110 210 4000 c000 c040 0 140928 741800 a
  //   b 1408a 1804 d03000 c22000 c00400 43000 e00110 210 4000 c000 c040 0 140928 741800 a b 1408a 1804
  //   d03000 c62000 c00400 43000 e00110 210 4000 c000 c040 0 140928 741800 a b 1408a 1804 d03000 c02000
  //   c00400 43000 e00110 210 4000 c000 c040 0 140928 741800 a b 1408a 1804 d03000 c02000 c00400 43000
  //   e00110 210 4000 c000 c040 0 140928 741800 a b 1408a 1804 d03000 c02000 c00400 43000 e00110 210 4000
  //   c000 c040 0 140928 741800 a b 1408a 1804 d03000 c02000 c00400 43000 e00110 210 4000 c000 c040 0
  //   140928 741800 a b 1408a 1804 d03000 c82000 c00400 43000 e00110 210 4000 c000 c040 0 140928 741800 a
  //   b 1408a 1804 d03000 c02000 c00400 43000 e00110 210 4000 c000 c040 0 140928 741800 a b 1408a 1804
  //   d03000 c02000 c00400 43000 e00110 210 4000 c000 c040 0 140928 741800 a b 1408a 1804 d03000 c02000
  //   c00400 43000 e00110 210 4000 c000 c040 0 140928 741800 a b 1408a 1804 d03000 c02000 c00400 43000
  //   e00110 210 4000 c000 c040 0 140928 741800 a b 1408a 1804 d03000 c02000 c00400 43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
endmodule
